// Logisim project alu.circ as structural Verilog: 1 circuit, main circuit alu
module alu (
  input  [31:0] A,
  input  [31:0] B,
  input  [3:0] ALUSel,
  output [31:0] ALUResult
);

  wire [31:0] add0, multiplier_1_cout, multiplier_1_out, multiplier_2_cout, or6, sll1, slt2, srl5, xor4;

  Shifter #(.shift("ar"), .width(32)) shifter_1 (.in(A), .\dist (B[4:0]), .out(sll1));
  assign or6 = A & B;  // AND_Gate and_1, 32 bits wide
  Multiplier #(.mode("twosComplement"), .width(32)) multiplier_1 (
    .a(A), .b(B), .out(multiplier_1_out), .cout(multiplier_1_cout));  // open: cin
  Multiplier #(.mode("twosComplement"), .width(32)) multiplier_2 (
    .a(A), .b(B), .cout(multiplier_2_cout));  // open: out, cin
  Subtractor #(.width(32)) subtractor_1 (.a(A), .b(B));  // open: out, bin, bout
  Adder #(.width(32)) adder_1 (.a(A), .b(B), .out(add0));  // open: cin, cout
  assign xor4 = A ^ B;  // XOR_Gate xor_1, 32 bits wide
  assign srl5 = A | B;  // OR_Gate or_1, 32 bits wide
  Multiplexer #(.enable("false"), .select(4), .width(32)) multiplexer_1 (
    .in0(add0), .in1(sll1), .in2(slt2), .in3({32{1'b0}}), .in4(xor4), .in5(srl5), .in10({32{1'b0}}),
    .in14({32{1'b0}}), .out(ALUResult), .sel(ALUSel));  // open: in6, in7, in8, in9, in11, in12, in13, in15

  // Notes on the sheet:
  //   INPUTS to your circuit
  //   DON'T CHANGE THE LOCATIONS OF THE INPUTS AND OUTPUTS!
  //   OUTPUT from your circuit
endmodule
